# Fritzing sketch Rpi3_ArduinoasISP_AT85_LED (saved by Fritzing 0.9.3b)
breadboards: 1

parts:
  Arduino_Mini_Pro_3_3v_8Mhz = Arduino Pro Mini v13
  U1 = attiny85 [package=dip]
  USB-TTL = FTDI Basic Programmer
  LED1 = LED - 3mm [color="Red (633nm)" package="3 mm [THT]"]
  R1 = Resistor [tolerance=±5% resistance=220 package=THT]
  R2 = Resistor [tolerance=±5% resistance=4.7k package=THT]
  Raspberry_Pi_1 = Raspberry Pi 3 [part_number=RPI-3-V1.2]  # not connected

nets:
  N1: Arduino_Mini_Pro_3_3v_8Mhz.DTR, USB-TTL.DTR
  N2: Arduino_Mini_Pro_3_3v_8Mhz.D0/TX, USB-TTL.RXI
  N3: Arduino_Mini_Pro_3_3v_8Mhz.D1/RX, USB-TTL.TXO
  N4: Arduino_Mini_Pro_3_3v_8Mhz.VCC, U1.Pin_8, USB-TTL.POWER, R2.Pin_0
  GND: Arduino_Mini_Pro_3_3v_8Mhz.GND, U1.Pin_4, USB-TTL.GND, R1.Pin_0
  N5: Arduino_Mini_Pro_3_3v_8Mhz.D13/SCK, U1.Pin_7
  N6: Arduino_Mini_Pro_3_3v_8Mhz.D12/MISO, U1.Pin_6
  N7: Arduino_Mini_Pro_3_3v_8Mhz.D11_PWM/MOSI, U1.Pin_5
  N8: Arduino_Mini_Pro_3_3v_8Mhz.D10_PWM/SS, U1.Pin_1, R2.Pin_1
  N9: U1.Pin_3, LED1.anode
  N10: LED1.cathode, R1.Pin_1

// code stored in the sketch: at85_flash_the_light.ino
#define LED_PIN 4
void setup()
{
        pinMode(LED_PIN, OUTPUT);
}

void loop()
{
        digitalWrite(LED_PIN, HIGH);
        delay(500);
        digitalWrite(LED_PIN, LOW);
        delay(500);
}
